// Logisim project Design.circ as structural Verilog
module S_R_Flip_Flop (
  input  S,
  input  Clock,
  input  R,
  output Q,
  output Q_prime
);

  wire nand_1_out, nand_2_out;

  nand nand_1 (nand_1_out, S, Clock);
  nand nand_2 (nand_2_out, Clock, R);
  nand nand_3 (Q, nand_1_out, Q_prime);
  nand nand_4 (Q_prime, Q, nand_2_out);
endmodule

module _1_bit_Register (
  input  Clock,
  input  D,
  input  Load,
  output Q
);

  wire and_1_out, and_2_out, not_1_out;

  not not_1 (not_1_out, D);
  and and_1 (and_1_out, D, Load);
  and and_2 (and_2_out, not_1_out, Load);
  S_R_Flip_Flop s_r_flip_flop_1 (.S(and_1_out), .Clock(Clock), .R(and_2_out), .Q(Q));  // open: Q_prime
endmodule

module _16_bit_Register (
);

  _1_bit_Register u_1_bit_register_1 ();  // open: Clock, D, Load, Q
  _1_bit_Register u_1_bit_register_2 ();  // open: Clock, D, Load, Q
  _1_bit_Register u_1_bit_register_3 ();  // open: Clock, D, Load, Q
  _1_bit_Register u_1_bit_register_4 ();  // open: Clock, D, Load, Q
  _1_bit_Register u_1_bit_register_5 ();  // open: Clock, D, Load, Q
  _1_bit_Register u_1_bit_register_6 ();  // open: Clock, D, Load, Q
  _1_bit_Register u_1_bit_register_7 ();  // open: Clock, D, Load, Q
  _1_bit_Register u_1_bit_register_8 ();  // open: Clock, D, Load, Q
  _1_bit_Register u_1_bit_register_9 ();  // open: Clock, D, Load, Q
  _1_bit_Register u_1_bit_register_10 ();  // open: Clock, D, Load, Q
  _1_bit_Register u_1_bit_register_11 ();  // open: Clock, D, Load, Q
  _1_bit_Register u_1_bit_register_12 ();  // open: Clock, D, Load, Q
  _1_bit_Register u_1_bit_register_13 ();  // open: Clock, D, Load, Q
  _1_bit_Register u_1_bit_register_14 ();  // open: Clock, D, Load, Q
  _1_bit_Register u_1_bit_register_15 ();  // open: Clock, D, Load, Q
  _1_bit_Register u_1_bit_register_16 ();  // open: Clock, D, Load, Q
endmodule
